# Fritzing sketch Untitled Sketch (saved by Fritzing 0.9.5d)
breadboards: 1

parts:
  WeMos_D1_Mini1 = WeMos D1 Mini
  M1 = Dagu DGServo 9g (Top view) [part_number=RS001B]
  Деталь1 = RFID-RC522-v2
  J2 = Piezo Speaker

nets:
  3V3: WeMos_D1_Mini1.3V3, Деталь1.3.3V
  5V: WeMos_D1_Mini1.5V, M1.vcc
  N1: WeMos_D1_Mini1.D2, Деталь1.SDA
  N2: WeMos_D1_Mini1.D3, J2.pin2
  N3: WeMos_D1_Mini1.D4, M1.pulse
  N4: WeMos_D1_Mini1.D5, Деталь1.SCK
  N5: WeMos_D1_Mini1.D6, Деталь1.MISO
  N6: WeMos_D1_Mini1.D7, Деталь1.MOSI
  N7: WeMos_D1_Mini1.G, M1.gnd, Деталь1.RST, J2.pin1

custom parts:
  RFID-RC522-v2: A simple China made RFID-RC522 Reader; do check the pin labels, as this is a MFRC522 based clone.
